# Fritzing sketch circuit (saved by Fritzing 0.9.0b)
breadboards: 1

parts:
  U1 = ESP8266 WiFi Module [part_number=ESP8266]
  Bauteil1 = Arduino Uno (Rev3)
  DHT1 = DHT11 Humitidy and Temperature Sensor
  R1 = Resistor [tolerance=±5% resistance=10k package=THT]
  Power_plug1 = Power plug

nets:
  N1: U1.RXD, Bauteil1.D0/RX
  VCC: U1.VCC, U1.CH_PD, DHT1.VDD, R1.Pin_1, Power_plug1.VCC
  N2: U1.GPIO_0, DHT1.DATA, R1.Pin_0
  GND: U1.GND, Bauteil1.GND, Bauteil1.RESET, DHT1.GND, Power_plug1.GND
  N3: U1.TXD, Bauteil1.D1/TX

notes:
  3.3V breadboard power supply
  ESP8266 can alternatively be connected to Arduino 3.3V line, it might not give enough peak power though
  DHT11
  ESP8266 / ESP-01
  Arduino UNO configured as USB to Serial device by connecting
  RESET and GND

custom parts:
  ESP8266 WiFi Module: Generic WiFi Module based on the ESP8266 with onboard PCB antenna and UART communications
  DHT11 Humitidy and Temperature Sensor: DHT11 Humidity and Temperature Sensor
